// Digital circuit 2_bit_adder.dig as structural Verilog
module _2_bit_adder (
  input  [1:0] a_2,
  input  [1:0] b_2,
  input  Carry_in,
  output Carry_out,
  output [1:0] Out_2
);

  wire full_adder_2_carry_out;

  Full_adder full_adder_1 (
    .carry_in(full_adder_2_carry_out), .b(b_2[1]), .a(a_2[1]), .sum(Out_2[1]), .carry_out(Carry_out));
  Full_adder full_adder_2 (
    .carry_in(Carry_in), .b(b_2[0]), .a(a_2[0]), .sum(Out_2[0]), .carry_out(full_adder_2_carry_out));
endmodule
