// Digital circuit 4_bit_adder.dig as structural Verilog
module _4_bit_adder (
  input  Carry_in,
  input  [3:0] b_4,
  input  [3:0] a_4,
  output out_0,
  output out_1,
  output out_2,
  output out_3,
  output Carry_out
);

  wire full_adder_2_carry_out, full_adder_3_carry_out, full_adder_4_carry_out;

  Full_adder full_adder_1 (
    .carry_in(full_adder_2_carry_out), .b(b_4[3]), .a(a_4[3]), .sum(out_3), .carry_out(Carry_out));
  Full_adder full_adder_2 (
    .carry_in(full_adder_3_carry_out), .b(b_4[2]), .a(a_4[2]), .sum(out_2), .carry_out(full_adder_2_carry_out));
  Full_adder full_adder_3 (
    .carry_in(full_adder_4_carry_out), .b(b_4[1]), .a(a_4[1]), .sum(out_1), .carry_out(full_adder_3_carry_out));
  Full_adder full_adder_4 (
    .carry_in(Carry_in), .b(b_4[0]), .a(a_4[0]), .sum(out_0), .carry_out(full_adder_4_carry_out));
endmodule
