// Digital circuit 8_bit_adder.dig as structural Verilog
module _8_bit_adder (
);

  _4_bit_adder _4_bit_adder_1 ();  // open: carry_in, b, a, out_0, out_1, out_2, out_3, carry_out
  _4_bit_adder _4_bit_adder_2 ();  // open: carry_in, b, a, out_0, out_1, out_2, out_3, carry_out
endmodule
