// Digital circuit Full_adder.dig as structural Verilog
module Full_adder (
  input  carry_in,
  input  b,
  input  a,
  output sum,
  output carry_out
);

  wire half_adder_1_carry, half_adder_1_sum, half_adder_2_carry;

  Half_adder half_adder_1 (.a(a), .b(b), .sum(half_adder_1_sum), .carry(half_adder_1_carry));
  Half_adder half_adder_2 (.a(carry_in), .b(half_adder_1_sum), .sum(sum), .carry(half_adder_2_carry));
  or or_1 (carry_out, half_adder_2_carry, half_adder_1_carry);
endmodule
