// Digital circuit Half_adder.dig as structural Verilog
module Half_adder (
  input  a,
  input  b,
  output sum,
  output carry
);

  XOR xor_1 (.a(a), .b(b), .out(sum));
  and and_1 (carry, a, b);
endmodule
