// Digital circuit part_2_adder.dig as structural Verilog
module part_2_adder (
  input  [3:0] a_4,
  input  [3:0] b_4,
  input  Carry_in,
  output [3:0] out_4,
  output Carry_out
);

  wire _2_bit_adder_2_carry_out;

  _2_bit_adder _2_bit_adder_1 (
    .a_2(a_4[3:2]), .b_2(b_4[3:2]), .Carry_in(_2_bit_adder_2_carry_out), .Carry_out(Carry_out),
    .Out_2(out_4[3:2]));
  _2_bit_adder _2_bit_adder_2 (
    .a_2(a_4[1:0]), .b_2(b_4[1:0]), .Carry_in(Carry_in), .Carry_out(_2_bit_adder_2_carry_out),
    .Out_2(out_4[1:0]));
endmodule
